// Digital circuit ASM4bit.dig as structural Verilog
module ASM4bit (
  input  [3:0] A,
  input  [3:0] B,
  input  [1:0] F,
  output S0,
  output S1,
  output S2,
  output S3,
  output S4,
  output S5,
  output S6,
  output S7
);

  ASM4 #(.applicationType("GHDL")) u_ASM4 (.A(A), .B(B), .F(F), .S({S7, S6, S5, S4, S3, S2, S1, S0}));
endmodule

/* Code of ASM4:
-- ASM4 stands for Adder-Subtracter-Multiplyer 4 bits

LIBRARY ieee;
USE ieee.std_logic_1164.all;
USE ieee.numeric_std.all;

entity ASM4 is
    port(
        A, B: in std_logic_vector(3 downto 0);
        F: in std_logic_vector(1 downto 0); -- Function selecting
        S: out std_logic_vector(7 downto 0)
    );
end ASM4;

architecture Equations of ASM4 is
    signal A_int, B_int, results: integer := 0;
    begin
        A_int <= to_integer(unsigned(A));
        B_int <= to_integer(unsigned(B));
        with F select
        results <= 
            A_int + B_int when "00",
            A_int - B_int when "01",
            A_int * B_int when "10",
            0 when others;
        S <= std_logic_vector(to_unsigned(results, 8));
end Equations;
*/
